# Fritzing sketch sensors (saved by Fritzing 0.9.2b)
breadboards: 1

parts:
  Part1 = Arduino Uno (Rev3)
  LED1 = LED - 5mm [color="Red (633nm)" package="5 mm [THT]"]
  R1 = Resistor [tolerance=±5% resistance=330 package=THT]
  PIR1 = PIR sensor
  Part2 = SRF05 Ultrasonic Rangefinder
  Part3 = Breakout Board for Electret Microphone  # not connected
  TiltSensor = PIR sensor

nets:
  N1: Part1.D8, Part2.Echo
  N2: Part1.D9_PWM, Part2.Trig
  N3: Part1.D10_PWM/SS, TiltSensor.SIG
  GND: Part1.GND, R1.Pin_0, PIR1.GND, Part2.GND, TiltSensor.GND
  N4: Part1.D6_PWM, LED1.anode
  N5: Part1.D7, PIR1.SIG
  VDD: Part1.5V, PIR1.VDD, Part2.VCC, TiltSensor.VDD
  N6: LED1.cathode, R1.Pin_1

notes:
  [write your note here]
  This a tilt sensor actually.
